# Fritzing sketch power-channel-p (saved by Fritzing 0.9.6b)
circuit board: 4.62597cm x 3.0402cm
breadboards: 1

parts:
  R1 = Resistor [tolerance=±5% resistance=150k package=THT]
  R2 = Resistor [tolerance=±5% resistance=680k package=THT]
  Q1 = Basic FET P-Channel [package="TO220 [THT]"]
  R3 = Resistor [tolerance=±5% resistance=220k package=THT]
  R4 = Resistor [tolerance=±5% resistance=10k package=THT]
  Q3 = NPN-Transistor [package="TO92 [THT]"]
  R5 = Resistor [tolerance=±5% resistance=150k package=THT]
  R6 = Resistor [tolerance=±5% resistance=10k package=THT]
  D1 = Rectifier Diode [part_number=1N4001 package="300 mil [THT]"]
  U1 = Voltage Regulator - 5V [package="TO220 [THT]"]
  C1 = Electrolytic Capacitor [capacitance=1µF voltage=35V package="100 mil [THT, electrolytic]"]
  J3 = female pin header, 1 pin [form="♀ (female)"]
  J4 = female pin header, 1 pin [form="♀ (female)"]
  J6 = female pin header, 1 pin [form="♀ (female)"]
  J7 = female pin header, 1 pin [form="♀ (female)"]
  J8 = female pin header, 1 pin [form="♀ (female)"]
  J9 = female pin header, 1 pin [form="♀ (female)"]
  J10 = female pin header, 1 pin [form="♀ (female)"]
  J11 = female pin header, 1 pin [form="♀ (female)"]
  R7 = Resistor [tolerance=±5% resistance=470k package=THT]
  Q2 = NPN-Transistor [package="TO92 [THT]"]
  Q4 = Basic FET P-Channel [package="TO220 [THT]"]
  R8 = Resistor [tolerance=±5% resistance=680k package=THT]
  R9 = Resistor [tolerance=±5% resistance=150k package=THT]
  C2 = Ceramic Capacitor [capacitance=100nF voltage=35V package="100 mil [THT, multilayer]"]
  R10 = Resistor [tolerance=±5% resistance=150k package=THT]
  J5 = female pin header, 1 pin [form="♀ (female)"]
  J12 = female pin header, 1 pin [form="♀ (female)"]
  D2 = Rectifier Diode [part_number=1N4001 package="300 mil [THT]"]

nets:
  N1: R1.Pin_0, Q1.source, J6.pin1, J5.pin1
  N2: R1.Pin_1, R2.Pin_0, Q1.gate
  N3: R2.Pin_1, Q2.C, D2.cathode
  N4: Q1.drain, R3.Pin_0, D1.cathode, J12.pin1
  N5: R3.Pin_1, R4.Pin_0
  N6: R4.Pin_1, R6.Pin_0, Q2.B
  GND: Q3.E, D1.anode, U1.GND, C1.-, J11.pin1, Q2.E, C2.0
  N7: Q3.B, R5.Pin_0
  N8: Q3.C, J9.pin1, R7.Pin_1
  N9: R5.Pin_1, C2.1, R10.Pin_0
  N10: R6.Pin_1, J10.pin1
  N11: U1.input_voltage, Q4.drain
  N12: U1.output_voltage, C1.+, J7.pin1
  N13: J3.pin1, R10.Pin_1
  N14: J4.pin1, Q4.source, R9.Pin_0
  N15: J8.pin1, R7.Pin_0
  N16: Q4.gate, R8.Pin_0, R9.Pin_1
  N17: R8.Pin_1, D2.anode

notes:
  +36V
  +5V
  charger
  battery +
  battery -
  +12~20V
  ADC
  off
  button
  S
  D
