# Fritzing sketch latch (saved by Fritzing 0.9.6b)
breadboards: 1

parts:
  J2 = female pin header, 2 pins [form="♀ (female)"]  # not connected
  R8 = Resistor [tolerance=±5% resistance=680k package=THT]  # not connected
  R9 = Resistor [tolerance=±5% resistance=47k package=THT]  # not connected
  R10 = Resistor [tolerance=±5% resistance=47k package=THT]  # not connected
  J3 = female pin header, 1 pin [form="♀ (female)"]  # not connected
  J7 = female pin header, 1 pin [form="♀ (female)"]  # not connected
  J8 = female pin header, 1 pin [form="♀ (female)"]  # not connected
  R13 = Resistor [tolerance=±5% resistance=680k package=THT]  # not connected
  R14 = Resistor [tolerance=±5% resistance=100k package=THT]  # not connected
  C4 = Ceramic Capacitor [capacitance=100nF voltage=35V package="100 mil [THT, multilayer]"]  # not connected
  J11 = female pin header, 1 pin [form="♀ (female)"]  # not connected
  R16 = Resistor [tolerance=±5% resistance=10k package=THT]  # not connected
  L1 = Inductor [inductance=330µH package="400 mil [THT]"]
  D9 = Schottky Diode [part_number=1N5817 package="300 mil [THT]"]  # not connected
  J10 = female pin header, 1 pin [form="♀ (female)"]  # not connected
  J12 = Piezo Speaker [part_number=PK-11N40PQ]  # not connected
  D10 = Diode [package=diode-1n4148]  # not connected
  Q6 = Basic FET N-Channel [part_number=IPB042N10N3GATMA1 package="D2Pak [SMD]"]  # not connected
  Q4 = PNP-Transistor [package="TO92 [THT]"]  # not connected
  J13 = female pin header, 1 pin [form="♀ (female)"]  # not connected
  Q7 = NPN-Transistor [part_number=BC337 package="TO92 [THT]"]  # not connected
  Q8 = NPN-Transistor [part_number=BC337 package="TO92 [THT]"]  # not connected
  J14 = female pin header, 1 pin [form="♀ (female)"]  # not connected
  C3 = Electrolytic Capacitor [capacitance=0.22mF voltage=6.3V package="200 mil [THT, electrolytic]"]

nets:
  N1: L1.pin_1, C3.+

notes:
  battery +36V
  off
  +5V
  ADC
  latching power control, https://www.edn.com/latching-power-switch-uses-momentary-pushbutton/, 2
  charger
  OUT
  IN
  levopen 2.0
  battery -
  motor -
