# Fritzing sketch latch (saved by Fritzing 0.9.6b)
circuit board: 4.49391cm x 3.49395cm
breadboards: 1

parts:
  R1 = Resistor [tolerance=±5% resistance=100k package=THT]
  Q1 = Basic FET P-Channel [package="TO220 [THT]"]
  J1 = female pin header, 2 pins [form="♀ (female)"]
  R2 = Resistor [tolerance=±5% resistance=470k package=THT]
  J2 = female pin header, 1 pin [form="♀ (female)"]
  R3 = Resistor [tolerance=±5% resistance=10k package=THT]
  D1 = Rectifier Diode [part_number=1N4001 package="300 mil [THT]"]
  R4 = Resistor [tolerance=±5% resistance=470k package=THT]
  Q2 = NPN-Transistor [package="TO92 [THT]"]
  C1 = Ceramic Capacitor [capacitance=100nF voltage=35V package="100 mil [THT, multilayer]"]
  R5 = Resistor [tolerance=±5% resistance=10k package=THT]
  R6 = Resistor [tolerance=±5% resistance=150k package=THT]
  Q3 = NPN-Transistor [package="TO92 [THT]"]
  R7 = Resistor [tolerance=±5% resistance=10k package=THT]
  J4 = female pin header, 1 pin [form="♀ (female)"]
  U2 = Voltage Regulator - 5V [package="TO220 [THT]"]
  D2 = Rectifier Diode [part_number=1N4001 package="300 mil [THT]"]
  Q4 = Basic FET P-Channel [package="TO220 [THT]"]
  R8 = Resistor [tolerance=±5% resistance=100k package=THT]
  R9 = Resistor [tolerance=±5% resistance=470k package=THT]
  D3 = Rectifier Diode [part_number=1N4001 package="300 mil [THT]"]
  C2 = Electrolytic Capacitor [capacitance=1µF voltage=35V package="100 mil [THT, electrolytic]"]
  J7 = female pin header, 1 pin [form="♀ (female)"]
  J3 = female pin header, 1 pin [form="♀ (female)"]
  J8 = female pin header, 1 pin [form="♀ (female)"]
  J6 = female pin header, 1 pin [form="♀ (female)"]
  J5 = female pin header, 1 pin [form="♀ (female)"]
  R10 = Resistor [tolerance=±5% resistance=10k package=THT]
  D4 = Rectifier Diode [part_number=1N4001 package="300 mil [THT]"]
  C3 = Ceramic Capacitor [capacitance=100nF voltage=35V package="100 mil [THT, multilayer]"]
  R11 = Resistor [tolerance=±5% resistance=150k package=THT]
  J9 = female pin header, 1 pin [form="♀ (female)"]
  C4 = Ceramic Capacitor [capacitance=100nF voltage=35V package="100 mil [THT, multilayer]"]

nets:
  N1: R1.Pin_0, Q1.source, J2.pin1
  N2: R1.Pin_1, Q1.gate, J1.pin2, R4.Pin_0
  N3: Q1.drain, R3.Pin_1, R6.Pin_0, D2.cathode, J5.pin1
  N4: J1.pin1, R2.Pin_0, D1.cathode, C1.1
  N5: R2.Pin_1, R3.Pin_0, D1.anode
  N6: R4.Pin_1, Q2.C, D3.cathode
  GND: Q2.E, C1.0, Q3.E, U2.GND, D2.anode, C2.-, J3.pin1, D4.anode, R11.Pin_1, C4.0
  N7: Q2.B, R5.Pin_0, R10.Pin_0
  N8: R5.Pin_1, R6.Pin_1, Q3.C, J7.pin1
  N9: Q3.B, R7.Pin_0
  N10: R7.Pin_1, J4.pin1, C4.1
  Vlow: U2.input_voltage, Q4.drain
  N11: U2.output_voltage, C2.+, J6.pin1
  N12: Q4.gate, R8.Pin_1, R9.Pin_0
  N13: Q4.source, R8.Pin_0, J8.pin1
  N14: R9.Pin_1, D3.anode
  N15: R10.Pin_1, D4.cathode, C3.0
  N16: C3.1, R11.Pin_0, J9.pin1

notes:
  battery +36V
  battery 0V
  +36V
  button
  charger
  off
  ADC
  +12~20V
  +5V
  latching power control, https://www.edn.com/latching-power-switch-uses-momentary-pushbutton/, 1
