# Fritzing sketch latch3 (saved by Fritzing 0.9.6b)
circuit board: 4.2cm x 3.5cm
breadboards: 1

parts:
  D2 = Rectifier Diode [part_number=1N4001 package="300 mil [THT]"]
  D4 = Rectifier Diode [part_number=1N4001 package="300 mil [THT]"]
  J2 = female pin header, 2 pins [form="♀ (female)"]
  Q2 = Basic FET P-Channel [package="TO220 [THT]"]
  R8 = Resistor [tolerance=±5% resistance=100k package=THT]
  R9 = Resistor [tolerance=±5% resistance=470k package=THT]
  Q4 = NPN-Transistor [part_number="BC337-25-AP\n" package="TO92 [THT]"]
  R10 = Resistor [tolerance=±5% resistance=10k package=THT]
  J3 = female pin header, 1 pin [form="♀ (female)"]
  J6 = female pin header, 1 pin [form="♀ (female)"]
  J7 = female pin header, 1 pin [form="♀ (female)"]
  J8 = female pin header, 1 pin [form="♀ (female)"]
  R13 = Resistor [tolerance=±5% resistance=150k package=THT]
  R14 = Resistor [tolerance=±5% resistance=10k package=THT]
  C4 = Ceramic Capacitor [capacitance=100nF voltage=35V package="100 mil [THT, multilayer]"]
  J11 = female pin header, 1 pin [form="♀ (female)"]
  R16 = Resistor [tolerance=±5% resistance=10k package=THT]
  L1 = Inductor [inductance=330µH package="400 mil [THT]"]
  D8 = Rectifier Diode [part_number=1N4001 package="300 mil [THT]"]
  D9 = Schottky Diode [part_number=1N5817 package="300 mil [THT]"]
  J10 = female pin header, 1 pin [form="♀ (female)"]
  U4 = Buck regulator LM7525 [part_number=LM2575 package=TO-263]
  C3 = Electrolytic Capacitor [capacitance=0.22mF voltage=6.3V package="1010 [SMD, electrolytic]"]
  J12 = Piezo Speaker [part_number=PK-11N40PQ]  # not connected
  Q5 = MOSFET-NCHANNEL [package=to-92]  # not connected

nets:
  N1: D2.cathode, D4.cathode, J2.pin2
  N2: D2.anode, R10.Pin_1, J7.pin1
  N3: D4.anode, R9.Pin_1, Q4.C
  GND: J2.pin1, Q4.E, R14.Pin_1, C4.0, D8.anode, D9.anode, U4.GND, U4./ON/OFF, C3.-
  N4: Q2.gate, R8.Pin_0, R9.Pin_0
  N5: Q2.drain, J6.pin1, R13.Pin_0, D8.cathode, U4.Vin
  N6: Q2.source, R8.Pin_1, J3.pin1
  N7: Q4.B, R10.Pin_0, R16.Pin_0
  N8: J8.pin1, L1.pin_0, U4.Feedback, C3.+
  N9: R13.Pin_1, R14.Pin_0, C4.1, J10.pin1
  N10: J11.pin1, R16.Pin_1
  N11: L1.pin_1, D9.cathode, U4.OUTPUT

notes:
  battery +36V
  +36V
  off
  +5V
  ADC
  latching power control, https://www.edn.com/latching-power-switch-uses-momentary-pushbutton/, 2
  charger
  OUT
  IN
  levopen 2.0

custom parts:
  Buck regulator LM7525: 5V DC Voltage Regulator - LM2575 LM2576
